// Logisim project cpu.circ as structural Verilog: 10 circuits, main circuit main
module main (
  output [31:0] RegDataW
);

  wire Br, MemRead, MemToReg, MemWrite, RegWrite;
  wire [3:0] ALUop;
  wire [4:0] ReadReg1, ReadReg2, ReadReg3, WriteReg;
  wire [23:0] Bdst;
  wire [31:0] ALUout, Instr, ReadDataM, RegData1, Regdata1_t, RegData2, Regdata2_t, RegData3, Regdata3_t,
       RegDataW_t, WriteDataM;

  Multiplexer #(.width(32)) multiplexer_1 (.in0(ALUout), .in1(ReadDataM), .out(RegDataW), .sel(MemToReg));
  PC pc_1 (.Bdst(Bdst), .Br(Br), .Instr(Instr));
  ControlUnit controlunit_1 (
    .Instr(Instr), .WriteDataM(WriteDataM), .ReadReg1(ReadReg1), .MemRead(MemRead), .ReadReg2(ReadReg2),
    .ReadReg3(ReadReg3), .WriteReg(WriteReg), .MemToReg(MemToReg), .MemWrite(MemWrite));  // open: LinkeReg, ALUsrc, Br, RegWrite, ALUop
  RegFile regfile_1 (
    .RegDataW(RegDataW_t), .RegWrite(RegWrite), .WriteReg(WriteReg), .ReadReg1(ReadReg1),
    .ReadReg2(ReadReg2), .ReadReg3(ReadReg3), .RegData1(RegData1), .RegData2(RegData2), .RegData3(RegData3));
  ALU alu_1 (
    .RegData1(Regdata1_t), .RegData2(Regdata2_t), .RegData3(Regdata3_t), .MemWrite(MemWrite),
    .MemRead(MemRead), .ALUop(ALUop), .Bdst(Bdst), .ALUout(ALUout));
  MEM mem_1 (.MemRead(MemRead), .MemWrite(MemWrite), .WriteDataM(WriteDataM), .ALUout(ALUout), .ReadDataM(ReadDataM));

  // Notes on the sheet:
  //   Stage 1: IF
  //   Stage 2: ID
  //   Stage 3: EX
  //   Stage 4: ME
  //   Stage 5: WB
endmodule

module PC (
  input  [23:0] Bdst,
  input  Br,
  output [31:0] Instr
);

  wire CLK;
  wire [23:0] adder_1_out, nextPC, PC;

  Clock clock_1 (.out(CLK));
  Register #(.width(24)) register_1 (.D(nextPC), .en(1'b1), .clk(CLK), .Q(PC));  // open: clr
  Adder #(.width(24)) adder_1 (.a(PC), .b(24'h1), .out(adder_1_out));  // open: cin, cout
  RAM #(.addrWidth(24), .dataWidth(32), .enables("line")) Instruction_Memory (
    .addr(PC), .we(1'b0), .clk(CLK), .dout(Instr));  // open: din
  Multiplexer #(.width(24)) multiplexer_1 (.in0(adder_1_out), .in1(Bdst), .out(nextPC), .sel(Br));
endmodule

module RegFile (
  input  [31:0] RegDataW,
  input  RegWrite,
  input  [4:0] WriteReg,
  input  [4:0] ReadReg1,
  input  [4:0] ReadReg2,
  input  [4:0] ReadReg3,
  output [31:0] RegData1,
  output [31:0] RegData2,
  output [31:0] RegData3
);

  wire CLK, WE0, WE1, WE2, WE3, WE4, WE5, WE6, WE7, WE8, WE9, WE10, WE11, WE12, WE13, WE14, WE15, WE16, WE17,
       WE18, WE19, WE20, WE21, WE22, WE23, WE24, WE25, WE26, WE27, WE28, WE29, WE30, WE31, WR0, WR1, WR2,
       WR3, WR4, WR5, WR6, WR7, WR8, WR9, WR10, WR11, WR12, WR13, WR14, WR15, WR16, WR17, WR18, WR19, WR20,
       WR21, WR22, WR23, WR24, WR25, WR26, WR27, WR28, WR29, WR30, WR31;
  wire [31:0] R0d, R1d, R2d, R3d, R4d, R5d, R6d, R7d, R8d, R9d, R10d, R11d, R12d, R13d, R14d, R15d, R16d,
       R17d, R18d, R19d, R20d, R21d, R22d, R23d, R24d, R25d, R26d, R27d, R28d, R29d, R30d, R31d;

  Decoder #(.select(5)) decoder_1 (
    .out0(WR0), .out1(WR1), .out2(WR2), .out3(WR3), .out4(WR4), .out5(WR5), .out6(WR6), .out7(WR7),
    .out8(WR8), .out9(WR9), .out10(WR10), .out11(WR11), .out12(WR12), .out13(WR13), .out14(WR14),
    .out15(WR15), .out16(WR16), .out17(WR17), .out18(WR18), .out19(WR19), .out20(WR20), .out21(WR21),
    .out22(WR22), .out23(WR23), .out24(WR24), .out25(WR25), .out26(WR26), .out27(WR27), .out28(WR28),
    .out29(WR29), .out30(WR30), .out31(WR31), .sel(WriteReg));  // open: en
  Clock clock_1 (.out(CLK));
  and and_1 (WE0, RegWrite, WR0);
  and and_2 (WE1, RegWrite, WR1);
  and and_3 (WE2, RegWrite, WR2);
  and and_4 (WE3, RegWrite, WR3);
  and and_5 (WE4, RegWrite, WR4);
  and and_6 (WE5, RegWrite, WR5);
  and and_7 (WE6, RegWrite, WR6);
  and and_8 (WE7, RegWrite, WR7);
  and and_9 (WE8, RegWrite, WR8);
  and and_10 (WE9, RegWrite, WR9);
  and and_11 (WE10, RegWrite, WR10);
  and and_12 (WE11, RegWrite, WR11);
  and and_13 (WE12, RegWrite, WR12);
  and and_14 (WE13, RegWrite, WR13);
  and and_15 (WE14, RegWrite, WR14);
  and and_16 (WE15, RegWrite, WR15);
  and and_17 (WE16, RegWrite, WR16);
  and and_18 (WE17, RegWrite, WR17);
  and and_19 (WE18, RegWrite, WR18);
  and and_20 (WE19, RegWrite, WR19);
  and and_21 (WE20, RegWrite, WR20);
  and and_22 (WE21, RegWrite, WR21);
  and and_23 (WE22, RegWrite, WR22);
  and and_24 (WE23, RegWrite, WR23);
  and and_25 (WE24, RegWrite, WR24);
  and and_26 (WE25, RegWrite, WR25);
  and and_27 (WE26, RegWrite, WR26);
  and and_28 (WR27, RegWrite, WR27);
  and and_29 (WR28, RegWrite, WR28);
  and and_30 (WR29, RegWrite, WR29);
  and and_31 (WE30, RegWrite, WR30);
  and and_32 (WE31, RegWrite, WR31);
  Register #(.width(32)) R0 (.D(RegDataW), .en(WE0), .clk(CLK), .Q(R0d));  // open: clr
  Register #(.width(32)) R1 (.D(RegDataW), .en(WE1), .clk(CLK), .Q(R1d));  // open: clr
  Register #(.width(32)) R2 (.D(RegDataW), .en(WE2), .clk(CLK), .Q(R2d));  // open: clr
  Register #(.width(32)) R3 (.D(RegDataW), .en(WE3), .clk(CLK), .Q(R3d));  // open: clr
  Register #(.width(32)) R4 (.D(RegDataW), .en(WE4), .clk(CLK), .Q(R4d));  // open: clr
  Register #(.width(32)) R5 (.D(RegDataW), .en(WE5), .clk(CLK), .Q(R5d));  // open: clr
  Register #(.width(32)) R6 (.D(RegDataW), .en(WE6), .clk(CLK), .Q(R6d));  // open: clr
  Register #(.width(32)) R7 (.D(RegDataW), .en(WE7), .clk(CLK), .Q(R7d));  // open: clr
  Multiplexer #(.select(5), .width(32)) multiplexer_1 (
    .in0(R0d), .in1(R1d), .in2(R2d), .in3(R3d), .in4(R4d), .in5(R5d), .in6(R6d), .in7(R7d), .in8(R8d),
    .in9(R9d), .in10(R10d), .in11(R11d), .in12(R12d), .in13(R13d), .in14(R14d), .in15(R15d), .in16(R16d),
    .in17(R17d), .in18(R18d), .in19(R19d), .in20(R20d), .in21(R21d), .in22(R22d), .in23(R23d), .in24(R24d),
    .in25(R25d), .in26(R26d), .in27(R27d), .in28(R28d), .in29(R29d), .in30(R30d), .in31(R31d),
    .out(RegData1), .sel(ReadReg1));
  Register #(.width(32)) R8 (.D(RegDataW), .en(WE8), .clk(CLK), .Q(R8d));  // open: clr
  Register #(.width(32)) R9 (.D(RegDataW), .en(WE9), .clk(CLK), .Q(R9d));  // open: clr
  Register #(.width(32)) R10 (.D(RegDataW), .en(WE10), .clk(CLK), .Q(R10d));  // open: clr
  Register #(.width(32)) R11 (.D(RegDataW), .en(WE11), .clk(CLK), .Q(R11d));  // open: clr
  Register #(.width(32)) R12 (.D(RegDataW), .en(WE12), .clk(CLK), .Q(R12d));  // open: clr
  Register #(.width(32)) R13 (.D(RegDataW), .en(WE13), .clk(CLK), .Q(R13d));  // open: clr
  Register #(.width(32)) R14 (.D(RegDataW), .en(WE14), .clk(CLK), .Q(R14d));  // open: clr
  Register #(.width(32)) R15 (.D(RegDataW), .en(WE15), .clk(CLK), .Q(R15d));  // open: clr
  Multiplexer #(.select(5), .width(32)) multiplexer_2 (
    .in0(R0d), .in1(R1d), .in2(R2d), .in3(R3d), .in4(R4d), .in5(R5d), .in6(R6d), .in7(R7d), .in8(R8d),
    .in9(R9d), .in10(R10d), .in11(R11d), .in12(R12d), .in13(R13d), .in14(R14d), .in15(R15d), .in16(R16d),
    .in17(R17d), .in18(R18d), .in19(R19d), .in20(R20d), .in21(R21d), .in22(R22d), .in23(R23d), .in24(R24d),
    .in25(R25d), .in26(R26d), .in27(R27d), .in28(R28d), .in29(R29d), .in30(R30d), .in31(R31d),
    .out(RegData3), .sel(ReadReg3));
  Register #(.width(32)) R16 (.D(RegDataW), .en(WE16), .clk(CLK), .Q(R16d));  // open: clr
  Register #(.width(32)) R17 (.D(RegDataW), .en(WE17), .clk(CLK), .Q(R17d));  // open: clr
  Register #(.width(32)) R18 (.D(RegDataW), .en(WE18), .clk(CLK), .Q(R18d));  // open: clr
  Register #(.width(32)) R19 (.D(RegDataW), .en(WE19), .clk(CLK), .Q(R19d));  // open: clr
  Register #(.width(32)) R20 (.D(RegDataW), .en(WE20), .clk(CLK), .Q(R20d));  // open: clr
  Register #(.width(32)) R21 (.D(RegDataW), .en(WE21), .clk(CLK), .Q(R21d));  // open: clr
  Register #(.width(32)) R22 (.D(RegDataW), .en(WE22), .clk(CLK), .Q(R22d));  // open: clr
  Register #(.width(32)) R23 (.D(RegDataW), .en(WE23), .clk(CLK), .Q(R23d));  // open: clr
  Multiplexer #(.select(5), .width(32)) multiplexer_3 (
    .in0(R0d), .in1(R1d), .in2(R2d), .in3(R3d), .in4(R4d), .in5(R5d), .in6(R6d), .in7(R7d), .in8(R8d),
    .in9(R9d), .in10(R10d), .in11(R11d), .in12(R12d), .in13(R13d), .in14(R14d), .in15(R15d), .in16(R16d),
    .in17(R17d), .in18(R18d), .in19(R19d), .in20(R20d), .in21(R21d), .in22(R22d), .in23(R23d), .in24(R24d),
    .in25(R25d), .in26(R26d), .in27(R27d), .in28(R28d), .in29(R29d), .in30(R30d), .in31(R31d),
    .out(RegData2), .sel(ReadReg2));
  Register #(.width(32)) R24 (.D(RegDataW), .en(WE24), .clk(CLK), .Q(R24d));  // open: clr
  Register #(.width(32)) R25 (.D(RegDataW), .en(WE25), .clk(CLK), .Q(R25d));  // open: clr
  Register #(.width(32)) R26 (.D(RegDataW), .en(WE26), .clk(CLK), .Q(R26d));  // open: clr
  Register #(.width(32)) R27 (.D(RegDataW), .en(WE27), .clk(CLK), .Q(R27d));  // open: clr
  Register #(.width(32)) R28 (.D(RegDataW), .en(WE28), .clk(CLK), .Q(R28d));  // open: clr
  Register #(.width(32)) R29 (.D(RegDataW), .en(WE29), .clk(CLK), .Q(R29d));  // open: clr
  Register #(.width(32)) R30_CMP (.D(RegDataW), .en(WE30), .clk(CLK), .Q(R30d));  // open: clr
  Register #(.width(32)) R31_LR (.D(RegDataW), .en(WE31), .clk(CLK), .Q(R31d));  // open: clr
endmodule

module ALU (
  input  [31:0] RegData1,
  input  [31:0] RegData2,
  input  [31:0] RegData3,
  input  MemWrite,
  input  MemRead,
  input  [3:0] ALUop,
  output [23:0] Bdst,
  output [31:0] ALUout
);

  wire [31:0] adder_1_out, ander_1_output1, divider_1_out, multiplier_1_out, negator_1_out, orer_1_output1,
       RegData2_t, shifter_1_out, shifter_2_out, shifter_3_out, subtractor_1_out, xorer_1_output1;

  Adder #(.width(32)) adder_1 (.a(RegData1), .b(RegData2_t), .out(adder_1_out));  // open: cin, cout
  Subtractor #(.width(32)) subtractor_1 (.a(RegData1), .b(RegData2_t), .out(subtractor_1_out));  // open: bin, bout
  Multiplier #(.width(32)) multiplier_1 (.a(RegData1), .b(RegData2_t), .out(multiplier_1_out));  // open: cin, cout
  Divider #(.width(32)) divider_1 (.a(RegData1), .b(RegData2_t), .out(divider_1_out));  // open: upper, rem
  ANDer ander_1 (.Input1(RegData1), .Input2(RegData2_t), .Output1(ander_1_output1));
  ORer orer_1 (.Input1(RegData1), .Input2(RegData2_t), .Output1(orer_1_output1));
  XORer xorer_1 (.Input1(RegData1), .Input2(RegData2_t), .Output1(xorer_1_output1));
  Shifter #(.width(32)) shifter_1 (.out(shifter_1_out));  // open: in, dist
  Shifter #(.shift("lr"), .width(32)) shifter_2 (.out(shifter_2_out));  // open: in, dist
  Shifter #(.shift("ar"), .width(32)) shifter_3 (.out(shifter_3_out));  // open: in, dist
  Negator #(.width(32)) negator_1 (.out(negator_1_out));  // open: in
  Multiplexer #(.select(4), .width(32)) multiplexer_1 (
    .in0(adder_1_out), .in1(subtractor_1_out), .in2(multiplier_1_out), .in3(divider_1_out),
    .in4(ander_1_output1), .in5(orer_1_output1), .in6(xorer_1_output1), .in7(shifter_1_out),
    .in8(shifter_2_out), .in9(shifter_3_out), .in10(negator_1_out), .out(ALUout), .sel(ALUop));  // open: in11, in12, in13, in14, in15

  assign RegData2 = RegData1;
  assign RegData3 = RegData1;

  // Notes on the sheet:
  //   0000 - ADD
  //   0001 - SUB
  //   0010 - MUL
  //   0011 - DIV
  //   0100 - AND
  //   0101 - ORR
  //   0110 - XOR
  //   0111 - LSL
  //   1000 - LSR
  //   1001 - ASR
  //   1010 - NEG
endmodule

module ControlUnit (
  input  [31:0] Instr,
  output [31:0] WriteDataM,
  output [4:0] ReadReg1,
  output MemRead,
  output [4:0] ReadReg2,
  output [4:0] ReadReg3,
  output [4:0] WriteReg,
  output LinkeReg,
  output MemToReg,
  output MemWrite,
  output [4:0] ALUsrc,
  output Br,
  output RegWrite,
  output [3:0] ALUop
);

  wire and_4_out, and_5_out, and_6_out, comparator_1_eq, comparator_2_eq, comparator_3_eq, comparator_4_eq,
       comparator_5_eq, comparator_6_eq, comparator_7_eq, comparator_8_eq, comparator_9_eq, comparator_10_eq,
       comparator_11_eq, comparator_12_eq, comparator_13_eq, comparator_14_eq, comparator_15_eq,
       comparator_16_eq, not_1_out;

  Comparator #(.width(1)) comparator_1 (.a(Instr[30]), .b(1'b1), .eq(comparator_1_eq));  // open: gt, lt
  Comparator #(.width(1)) comparator_2 (.a(Instr[31]), .b(1'b0), .eq(comparator_2_eq));  // open: gt, lt
  Comparator #(.width(1)) comparator_3 (.a(Instr[26]), .b(1'b0), .eq(comparator_3_eq));  // open: gt, lt
  Comparator #(.width(1)) comparator_4 (.a(Instr[30]), .b(1'b1), .eq(comparator_4_eq));  // open: gt, lt
  Comparator #(.width(1)) comparator_5 (.a(Instr[31]), .b(1'b0), .eq(comparator_5_eq));  // open: gt, lt
  Comparator #(.width(1)) comparator_6 (.a(Instr[26]), .b(1'b1), .eq(comparator_6_eq));  // open: gt, lt
  Comparator #(.width(1)) comparator_7 (.a(Instr[30]), .b(1'b0), .eq(comparator_7_eq));  // open: gt, lt
  Comparator #(.width(1)) comparator_8 (.a(Instr[31]), .b(1'b1), .eq(comparator_8_eq));  // open: gt, lt
  Comparator #(.width(1)) comparator_9 (.a(Instr[31]), .b(1'b0), .eq(comparator_9_eq));  // open: gt, lt
  Comparator #(.width(1)) comparator_10 (.a(Instr[30]), .b(1'b0), .eq(comparator_10_eq));  // open: gt, lt
  Comparator #(.width(1)) comparator_11 (.a(Instr[31]), .b(1'b0), .eq(comparator_11_eq));  // open: gt, lt
  Comparator #(.width(1)) comparator_12 (.a(Instr[30]), .b(1'b1), .eq(comparator_12_eq));  // open: gt, lt
  not not_1 (not_1_out, comparator_13_eq);
  Comparator #(.width(1)) comparator_13 (.a(Instr[26]), .b(1'b1), .eq(comparator_13_eq));  // open: gt, lt
  Comparator #(.width(1)) comparator_14 (.a(Instr[31]), .b(1'b1), .eq(comparator_14_eq));  // open: gt, lt
  Comparator #(.width(1)) comparator_15 (.a(Instr[30]), .b(1'b1), .eq(comparator_15_eq));  // open: gt, lt
  Comparator #(.width(1)) comparator_16 (.a(Instr[27]), .b(1'b1), .eq(comparator_16_eq));  // open: gt, lt
  and and_1 (MemRead, comparator_1_eq, comparator_2_eq, comparator_3_eq);
  and and_2 (MemWrite, comparator_4_eq, comparator_5_eq, comparator_6_eq);
  and and_3 (Br, comparator_7_eq, comparator_8_eq);
  and and_4 (and_4_out, comparator_9_eq, comparator_10_eq);
  and and_5 (and_5_out, comparator_11_eq, not_1_out);
  and and_6 (and_6_out, comparator_14_eq, comparator_16_eq);
  or or_1 (RegWrite, and_4_out, and_5_out, and_6_out);

  assign ALUop = Instr[29:26];

  // Notes on the sheet:
  //   Opcode
  //   B/BEQ/...?
  //   Arithmetic?
  //   LDR, ADR?
  //   MOV?
  //   LDR or STR?
  //   0000 - ADD
  //   0001 - SUB
  //   0010 - MUL
  //   0011 - DIV
  //   0100 - AND
  //   0101 - ORR
  //   0110 - XOR
  //   0111 - LSL
  //   1000 - LSR
  //   1001 - ASR
  //   1010 - NEG
  //   LDR
  //   STR
  //   Instr w/o Opcode
endmodule

module MEM (
  input  MemRead,
  input  MemWrite,
  input  [31:0] WriteDataM,
  input  [31:0] ALUout,
  output [31:0] ReadDataM
);

  wire CLK;
  wire [23:0] bit_extender_1_out;
  wire [31:0] ReadDataM_t;

  Clock clock_1 (.out(CLK));
  Bit_Extender #(.in_width(32), .out_width(24)) bit_extender_1 (.in(ALUout), .out(bit_extender_1_out));
  RAM #(.addrWidth(24), .dataWidth(32), .enables("line")) DRAM (
    .addr(bit_extender_1_out), .we(MemRead), .clk(CLK), .din(WriteDataM), .dout(ReadDataM_t));
  cache cache_1 (.Address(bit_extender_1_out), .DataIn(ReadDataM_t), .DataOut(ReadDataM));
endmodule

// Out
module ANDer (
  input  [31:0] Input1,
  input  [31:0] Input2,
  output [31:0] Output1
);

  and and_1 (Output1[31], Input1[31], Input2[31]);
  and and_2 (Output1[15], Input1[15], Input2[15]);
  and and_3 (Output1[30], Input1[30], Input2[30]);
  and and_4 (Output1[14], Input1[14], Input2[14]);
  and and_5 (Output1[29], Input1[29], Input2[29]);
  and and_6 (Output1[13], Input1[13], Input2[13]);
  and and_7 (Output1[28], Input1[28], Input2[28]);
  and and_8 (Output1[12], Input1[12], Input2[12]);
  and and_9 (Output1[27], Input1[27], Input2[27]);
  and and_10 (Output1[11], Input1[11], Input2[11]);
  and and_11 (Output1[26], Input1[26], Input2[26]);
  and and_12 (Output1[10], Input1[10], Input2[10]);
  and and_13 (Output1[25], Input1[25], Input2[25]);
  and and_14 (Output1[9], Input1[9], Input2[9]);
  and and_15 (Output1[24], Input1[24], Input2[24]);
  and and_16 (Output1[8], Input1[8], Input2[8]);
  and and_17 (Output1[23], Input1[23], Input2[23]);
  and and_18 (Output1[7], Input1[7], Input2[7]);
  and and_19 (Output1[22], Input1[22], Input2[22]);
  and and_20 (Output1[6], Input1[6], Input2[6]);
  and and_21 (Output1[21], Input1[21], Input2[21]);
  and and_22 (Output1[5], Input1[5], Input2[5]);
  and and_23 (Output1[20], Input1[20], Input2[20]);
  and and_24 (Output1[4], Input1[4], Input2[4]);
  and and_25 (Output1[19], Input1[19], Input2[19]);
  and and_26 (Output1[3], Input1[3], Input2[3]);
  and and_27 (Output1[18], Input1[18], Input2[18]);
  and and_28 (Output1[2], Input1[2], Input2[2]);
  and and_29 (Output1[17], Input1[17], Input2[17]);
  and and_30 (Output1[1], Input1[1], Input2[1]);
  and and_31 (Output1[16], Input1[16], Input2[16]);
  and and_32 (Output1[0], Input1[0], Input2[0]);

  // Other names for the same wires on the sheet: I100 = Input1[0]; I101 = Input1[1]; I102 = Input1[2];
  //   I103 = Input1[3]; I104 = Input1[4]; I105 = Input1[5]; I106 = Input1[6]; I107 = Input1[7]; I108 = Input1[8];
  //   I109 = Input1[9]; I110 = Input1[10]; I111 = Input1[11]; I112 = Input1[12]; I113 = Input1[13]; I114 = Input1[14];
  //   I115 = Input1[15]; I116 = Input1[16]; I117 = Input1[17]; I118 = Input1[18]; I119 = Input1[19];
  //   I120 = Input1[20]; I121 = Input1[21]; I122 = Input1[22]; I123 = Input1[23]; I124 = Input1[24];
  //   I125 = Input1[25]; I126 = Input1[26]; I127 = Input1[27]; I128 = Input1[28]; I129 = Input1[29];
  //   I130 = Input1[30]; I131 = Input1[31]; I200 = Input2[0]; I201 = Input2[1]; I202 = Input2[2]; I203 = Input2[3];
  //   I204 = Input2[4]; I205 = Input2[5]; I206 = Input2[6]; I207 = Input2[7]; I208 = Input2[8]; I209 = Input2[9];
  //   I210 = Input2[10]; I211 = Input2[11]; I212 = Input2[12]; I213 = Input2[13]; I214 = Input2[14];
  //   I215 = Input2[15]; I216 = Input2[16]; I217 = Input2[17]; I218 = Input2[18]; I219 = Input2[19];
  //   I220 = Input2[20]; I221 = Input2[21]; I222 = Input2[22]; I223 = Input2[23]; I224 = Input2[24];
  //   I225 = Input2[25]; I226 = Input2[26]; I227 = Input2[27]; I228 = Input2[28]; I229 = Input2[29];
  //   I230 = Input2[30]; I231 = Input2[31]; O00 = Output1[0]; O01 = Output1[1]; O02 = Output1[2]; O03 = Output1[3];
  //   O04 = Output1[4]; O05 = Output1[5]; O06 = Output1[6]; O07 = Output1[7]; O08 = Output1[8]; O09 = Output1[9];
  //   O10 = Output1[10]; O11 = Output1[11]; O12 = Output1[12]; O13 = Output1[13]; O14 = Output1[14];
  //   O15 = Output1[15]; O16 = Output1[16]; O17 = Output1[17]; O18 = Output1[18]; O19 = Output1[19];
  //   O20 = Output1[20]; O21 = Output1[21]; O22 = Output1[22]; O23 = Output1[23]; O24 = Output1[24];
  //   O25 = Output1[25]; O26 = Output1[26]; O27 = Output1[27]; O28 = Output1[28]; O29 = Output1[29];
  //   O30 = Output1[30]; O31 = Output1[31]
endmodule

module ORer (
  input  [31:0] Input1,
  input  [31:0] Input2,
  output [31:0] Output1
);

  or or_1 (Output1[31], Input1[31], Input2[31]);
  or or_2 (Output1[15], Input1[15], Input2[15]);
  or or_3 (Output1[30], Input1[30], Input2[30]);
  or or_4 (Output1[14], Input1[14], Input2[14]);
  or or_5 (Output1[29], Input1[29], Input2[29]);
  or or_6 (Output1[13], Input1[13], Input2[13]);
  or or_7 (Output1[28], Input1[28], Input2[28]);
  or or_8 (Output1[12], Input1[12], Input2[12]);
  or or_9 (Output1[27], Input1[27], Input2[27]);
  or or_10 (Output1[11], Input1[11], Input2[11]);
  or or_11 (Output1[26], Input1[26], Input2[26]);
  or or_12 (Output1[10], Input1[10], Input2[10]);
  or or_13 (Output1[25], Input1[25], Input2[25]);
  or or_14 (Output1[9], Input1[9], Input2[9]);
  or or_15 (Output1[24], Input1[24], Input2[24]);
  or or_16 (Output1[8], Input1[8], Input2[8]);
  or or_17 (Output1[23], Input1[23], Input2[23]);
  or or_18 (Output1[7], Input1[7], Input2[7]);
  or or_19 (Output1[22], Input1[22], Input2[22]);
  or or_20 (Output1[6], Input1[6], Input2[6]);
  or or_21 (Output1[21], Input1[21], Input2[21]);
  or or_22 (Output1[5], Input1[5], Input2[5]);
  or or_23 (Output1[20], Input1[20], Input2[20]);
  or or_24 (Output1[4], Input1[4], Input2[4]);
  or or_25 (Output1[19], Input1[19], Input2[19]);
  or or_26 (Output1[3], Input1[3], Input2[3]);
  or or_27 (Output1[18], Input1[18], Input2[18]);
  or or_28 (Output1[2], Input1[2], Input2[2]);
  or or_29 (Output1[17], Input1[17], Input2[17]);
  or or_30 (Output1[1], Input1[1], Input2[1]);
  or or_31 (Output1[16], Input1[16], Input2[16]);
  or or_32 (Output1[0], Input1[0], Input2[0]);

  // Other names for the same wires on the sheet: I100 = Input1[0]; I101 = Input1[1]; I102 = Input1[2];
  //   I103 = Input1[3]; I104 = Input1[4]; I105 = Input1[5]; I106 = Input1[6]; I107 = Input1[7]; I108 = Input1[8];
  //   I109 = Input1[9]; I110 = Input1[10]; I111 = Input1[11]; I112 = Input1[12]; I113 = Input1[13]; I114 = Input1[14];
  //   I115 = Input1[15]; I116 = Input1[16]; I117 = Input1[17]; I118 = Input1[18]; I119 = Input1[19];
  //   I120 = Input1[20]; I121 = Input1[21]; I122 = Input1[22]; I123 = Input1[23]; I124 = Input1[24];
  //   I125 = Input1[25]; I126 = Input1[26]; I127 = Input1[27]; I128 = Input1[28]; I129 = Input1[29];
  //   I130 = Input1[30]; I131 = Input1[31]; I200 = Input2[0]; I201 = Input2[1]; I202 = Input2[2]; I203 = Input2[3];
  //   I204 = Input2[4]; I205 = Input2[5]; I206 = Input2[6]; I207 = Input2[7]; I208 = Input2[8]; I209 = Input2[9];
  //   I210 = Input2[10]; I211 = Input2[11]; I212 = Input2[12]; I213 = Input2[13]; I214 = Input2[14];
  //   I215 = Input2[15]; I216 = Input2[16]; I217 = Input2[17]; I218 = Input2[18]; I219 = Input2[19];
  //   I220 = Input2[20]; I221 = Input2[21]; I222 = Input2[22]; I223 = Input2[23]; I224 = Input2[24];
  //   I225 = Input2[25]; I226 = Input2[26]; I227 = Input2[27]; I228 = Input2[28]; I229 = Input2[29];
  //   I230 = Input2[30]; I231 = Input2[31]; O00 = Output1[0]; O01 = Output1[1]; O02 = Output1[2]; O03 = Output1[3];
  //   O04 = Output1[4]; O05 = Output1[5]; O06 = Output1[6]; O07 = Output1[7]; O08 = Output1[8]; O09 = Output1[9];
  //   O10 = Output1[10]; O11 = Output1[11]; O12 = Output1[12]; O13 = Output1[13]; O14 = Output1[14];
  //   O15 = Output1[15]; O16 = Output1[16]; O17 = Output1[17]; O18 = Output1[18]; O19 = Output1[19];
  //   O20 = Output1[20]; O21 = Output1[21]; O22 = Output1[22]; O23 = Output1[23]; O24 = Output1[24];
  //   O25 = Output1[25]; O26 = Output1[26]; O27 = Output1[27]; O28 = Output1[28]; O29 = Output1[29];
  //   O30 = Output1[30]; O31 = Output1[31]
endmodule

module XORer (
  input  [31:0] Input1,
  input  [31:0] Input2,
  output [31:0] Output1
);

  xor xor_1 (Output1[31], Input1[31], Input2[31]);
  xor xor_2 (Output1[15], Input1[15], Input2[15]);
  xor xor_3 (Output1[30], Input1[30], Input2[30]);
  xor xor_4 (Output1[14], Input1[14], Input2[14]);
  xor xor_5 (Output1[29], Input1[29], Input2[29]);
  xor xor_6 (Output1[13], Input1[13], Input2[13]);
  xor xor_7 (Output1[28], Input1[28], Input2[28]);
  xor xor_8 (Output1[12], Input1[12], Input2[12]);
  xor xor_9 (Output1[27], Input1[27], Input2[27]);
  xor xor_10 (Output1[11], Input1[11], Input2[11]);
  xor xor_11 (Output1[26], Input1[26], Input2[26]);
  xor xor_12 (Output1[10], Input1[10], Input2[10]);
  xor xor_13 (Output1[25], Input1[25], Input2[25]);
  xor xor_14 (Output1[9], Input1[9], Input2[9]);
  xor xor_15 (Output1[24], Input1[24], Input2[24]);
  xor xor_16 (Output1[8], Input1[8], Input2[8]);
  xor xor_17 (Output1[23], Input1[23], Input2[23]);
  xor xor_18 (Output1[7], Input1[7], Input2[7]);
  xor xor_19 (Output1[22], Input1[22], Input2[22]);
  xor xor_20 (Output1[6], Input1[6], Input2[6]);
  xor xor_21 (Output1[21], Input1[21], Input2[21]);
  xor xor_22 (Output1[5], Input1[5], Input2[5]);
  xor xor_23 (Output1[20], Input1[20], Input2[20]);
  xor xor_24 (Output1[4], Input1[4], Input2[4]);
  xor xor_25 (Output1[19], Input1[19], Input2[19]);
  xor xor_26 (Output1[3], Input1[3], Input2[3]);
  xor xor_27 (Output1[18], Input1[18], Input2[18]);
  xor xor_28 (Output1[2], Input1[2], Input2[2]);
  xor xor_29 (Output1[17], Input1[17], Input2[17]);
  xor xor_30 (Output1[1], Input1[1], Input2[1]);
  xor xor_31 (Output1[16], Input1[16], Input2[16]);
  xor xor_32 (Output1[0], Input1[0], Input2[0]);

  // Other names for the same wires on the sheet: I100 = Input1[0]; I101 = Input1[1]; I102 = Input1[2];
  //   I103 = Input1[3]; I104 = Input1[4]; I105 = Input1[5]; I106 = Input1[6]; I107 = Input1[7]; I108 = Input1[8];
  //   I109 = Input1[9]; I110 = Input1[10]; I111 = Input1[11]; I112 = Input1[12]; I113 = Input1[13]; I114 = Input1[14];
  //   I115 = Input1[15]; I116 = Input1[16]; I117 = Input1[17]; I118 = Input1[18]; I119 = Input1[19];
  //   I120 = Input1[20]; I121 = Input1[21]; I122 = Input1[22]; I123 = Input1[23]; I124 = Input1[24];
  //   I125 = Input1[25]; I126 = Input1[26]; I127 = Input1[27]; I128 = Input1[28]; I129 = Input1[29];
  //   I130 = Input1[30]; I131 = Input1[31]; I200 = Input2[0]; I201 = Input2[1]; I202 = Input2[2]; I203 = Input2[3];
  //   I204 = Input2[4]; I205 = Input2[5]; I206 = Input2[6]; I207 = Input2[7]; I208 = Input2[8]; I209 = Input2[9];
  //   I210 = Input2[10]; I211 = Input2[11]; I212 = Input2[12]; I213 = Input2[13]; I214 = Input2[14];
  //   I215 = Input2[15]; I216 = Input2[16]; I217 = Input2[17]; I218 = Input2[18]; I219 = Input2[19];
  //   I220 = Input2[20]; I221 = Input2[21]; I222 = Input2[22]; I223 = Input2[23]; I224 = Input2[24];
  //   I225 = Input2[25]; I226 = Input2[26]; I227 = Input2[27]; I228 = Input2[28]; I229 = Input2[29];
  //   I230 = Input2[30]; I231 = Input2[31]; O00 = Output1[0]; O01 = Output1[1]; O02 = Output1[2]; O03 = Output1[3];
  //   O04 = Output1[4]; O05 = Output1[5]; O06 = Output1[6]; O07 = Output1[7]; O08 = Output1[8]; O09 = Output1[9];
  //   O10 = Output1[10]; O11 = Output1[11]; O12 = Output1[12]; O13 = Output1[13]; O14 = Output1[14];
  //   O15 = Output1[15]; O16 = Output1[16]; O17 = Output1[17]; O18 = Output1[18]; O19 = Output1[19];
  //   O20 = Output1[20]; O21 = Output1[21]; O22 = Output1[22]; O23 = Output1[23]; O24 = Output1[24];
  //   O25 = Output1[25]; O26 = Output1[26]; O27 = Output1[27]; O28 = Output1[28]; O29 = Output1[29];
  //   O30 = Output1[30]; O31 = Output1[31]
endmodule

module cache (
  input  [23:0] Address,
  input  [31:0] DataIn,
  output [31:0] DataOut
);

  wire and_1_out, CLK, comparator_1_eq, Miss, ValidBit;
  wire [15:0] StoredTag;
  wire [31:0] CacheData;

  Clock clock_1 (.out(CLK));
  RAM #(.dataWidth(16), .enables("line")) TagMemory (
    .addr(Address[7:0]), .we(Miss), .clk(CLK), .din(Address[23:8]), .dout(StoredTag));
  RAM #(.dataWidth(1), .enables("line")) ValidBitMemory (
    .addr(Address[7:0]), .we(Miss), .clk(CLK), .din(1'b1), .dout(ValidBit));
  Comparator #(.width(16)) comparator_1 (.a(Address[23:8]), .b(StoredTag), .eq(comparator_1_eq));  // open: gt, lt
  and and_1 (and_1_out, comparator_1_eq, ValidBit);
  Multiplexer #(.width(32)) multiplexer_1 (.in0(DataIn), .in1(CacheData), .out(DataOut), .sel(and_1_out));
  not not_1 (Miss, and_1_out);
  RAM #(.dataWidth(32), .enables("line")) DataMemory (
    .addr(Address[7:0]), .we(Miss), .clk(CLK), .din(DataIn), .dout(CacheData));

  // Other names for the same wires on the sheet: Index[7:0] = Address[7:0]; Tag[15:0] = Address[23:8]
endmodule
